# Fritzing sketch ledquiclignote_croquis (saved by Fritzing 0.9.3b)
breadboards: 1

parts:
  LED1 = LED - 5mm [color="Red (633nm)" package="5 mm [THT]"]
  R1 = Resistor [tolerance=±5% resistance=220 package=THT]
  Composant1 = Arduino Uno (Rev3)

nets:
  N1: LED1.cathode, Composant1.GND
  N2: LED1.anode, R1.Pin_0
  N3: R1.Pin_1, Composant1.D13/SCK
