# Fritzing sketch termometre (saved by Fritzing 0.9.3b)
circuit board: 8.46667cm x 5.64444cm
breadboards: 1

parts:
  T1 = LM34 Temperature Sensor [package="TO92 [THT]"]
  Composant1 = Arduino Uno (Rev3)
  LED1 = 7-SEGMENT-4DIGIT-YOUNGSUN [package=7-segment-4digit-youngsun-longpads]
  R1 = Resistor [tolerance=±5% resistance=220 package=THT]
  R9 = Resistor [tolerance=±5% resistance=1k package=THT]
  R10 = Resistor [tolerance=±5% resistance=1k package=THT]
  R11 = Resistor [tolerance=±5% resistance=1k package=THT]
  R12 = Resistor [tolerance=±5% resistance=1k package=THT]
  R13 = Resistor [tolerance=±5% resistance=1k package=THT]
  R14 = Resistor [tolerance=±5% resistance=1k package=THT]
  LED2 = LED - 5mm [color="Red (633nm)" package="5 mm [THT]"]
  R15 = Resistor [tolerance=±5% resistance=220 package=THT]

nets:
  N1: T1.+Vs, Composant1.5V
  N2: T1.Vout, R1.Pin_0
  GND: T1.GND, Composant1.GND, LED2.cathode
  N3: Composant1.A0, LED1.C, R1.Pin_1, R12.Pin_1
  N4: Composant1.D8, R13.Pin_0
  N5: Composant1.D9_PWM, R14.Pin_0
  N6: Composant1.D10_PWM/SS, LED1.DIG4
  N7: Composant1.D11_PWM/MOSI, LED1.DIG3
  N8: Composant1.D12/MISO, LED1.DIG2
  N9: Composant1.D13/SCK, LED1.DIG1
  N10: Composant1.D2, R15.Pin_1
  N11: Composant1.D4, R9.Pin_0
  N12: Composant1.D5_PWM, R10.Pin_0
  N13: Composant1.D6_PWM, R11.Pin_0
  N14: Composant1.D7, R12.Pin_0
  N15: LED1.D, R11.Pin_1
  N16: LED1.E, R10.Pin_1
  N17: LED1.F, R9.Pin_1
  N18: LED1.A, R14.Pin_1
  N19: LED1.B, R13.Pin_1
  N20: LED2.anode, R15.Pin_0

// code stored in the sketch: termo.ino
int x;
int del = 2;
int val;
int temp;
int diz;
int uni;
int boucle;

void setup() {
  pinMode(13, OUTPUT);
  pinMode(12, OUTPUT);
  pinMode(11, OUTPUT);
  pinMode(10, OUTPUT);
  pinMode(9, OUTPUT);
  pinMode(8, OUTPUT);
  pinMode(7, OUTPUT);
  pinMode(6, OUTPUT);
  pinMode(5, OUTPUT);
  pinMode(4, OUTPUT);
  pinMode(3, OUTPUT);

}

void loop() {
  val = analogRead(0);
  temp=(500*val)/1024;;
  diz = temp/10;
  uni=temp%10;
  boucle=0;
  while(boucle<200){
    digitalWrite(13, HIGH);
    affdigit(diz);
    delay(del);
    digitalWrite(13, LOW);
    digitalWrite(12, HIGH);
    affdigit(uni);
    delay(del);
    digitalWrite(12, LOW);
    digitalWrite(11, HIGH);
    degres();
    delay(del);
    digitalWrite(11, LOW);
    digitalWrite(10, HIGH);
    C();
    delay(del);
    digitalWrite(10, LOW);
    if(temp>=21||temp=<17){
    digitalWrite(2, HIGH);
    }
    boucle++;
  }
}

void affdigit(int x){
  switch(x){
    case 1:un();break;
    case 2:deux();break;
    case 3:trois();break;
    case 4:quatre();break;
    case 5:cinq();break;
    case 6:six();break;
    case 7:sept();break;
    case 8:huit();break;
    case 9:neuf();break;
    default:zero();break;
  }
}

void degres(){
  digitalWrite(9, LOW);
  digitalWrite(8, LOW);
  digitalWrite(7, HIGH);
  digitalWrite(6, HIGH);
  digitalWrite(5, HIGH);
  digitalWrite(4, LOW);
  digitalWrite(3, LOW);
}

void C(){
  digitalWrite(9, LOW);
  digitalWrite(8, HIGH);
  digitalWrite(7, HIGH);
  digitalWrite(6, LOW);
  digitalWrite(5, LOW);
  digitalWrite(4, LOW);
  digitalWrite(3, HIGH);
}

void un(){
  digitalWrite(9, HIGH);
  digitalWrite(8, LOW);
  digitalWrite(7, LOW);
  digitalWrite(6, HIGH);
  digitalWrite(5, HIGH);
  digitalWrite(4, HIGH);
  digitalWrite(3, HIGH);
}

void deux(){
  digitalWrite(9, LOW);
  digitalWrite(8, LOW);
  digitalWrite(7, HIGH);
  digitalWrite(6, LOW);
  digitalWrite(5, LOW);
  digitalWrite(4, HIGH);
  digitalWrite(3, LOW);
}

void trois(){
  digitalWrite(9, LOW);
  digitalWrite(8, LOW);
  digitalWrite(7, LOW);
  digitalWrite(6, LOW);
  digitalWrite(5, HIGH);
  digitalWrite(4, HIGH);
  digitalWrite(3, LOW);
}

void quatre(){
  digitalWrite(9, HIGH);
  digitalWrite(8, LOW);
  digitalWrite(7, LOW);
  digitalWrite(6, HIGH);
  digitalWrite(5, HIGH);
  digitalWrite(4, LOW);
  digitalWrite(3, LOW);
}

void cinq(){
  digitalWrite(9, LOW);
  digitalWrite(8, HIGH);
  digitalWrite(7, LOW);
  digitalWrite(6, LOW);
  digitalWrite(5, HIGH);
  digitalWrite(4, LOW);
  digitalWrite(3, LOW);
}

void six(){
  digitalWrite(9, LOW);
  digitalWrite(8, HIGH);
  digitalWrite(7, LOW);
  digitalWrite(6, LOW);
  digitalWrite(5, LOW);
  digitalWrite(4, LOW);
  digitalWrite(3, LOW);
}

void sept(){
  digitalWrite(9, LOW);
  digitalWrite(8, LOW);
  digitalWrite(7, LOW);
  digitalWrite(6, HIGH);
  digitalWrite(5, HIGH);
  digitalWrite(4, HIGH);
  digitalWrite(3, HIGH);
}

void huit(){
  digitalWrite(9, LOW);
  digitalWrite(8, LOW);
  digitalWrite(7, LOW);
  digitalWrite(6, LOW);
  digitalWrite(5, LOW);
  digitalWrite(4, LOW);
  digitalWrite(3, LOW);
}

void neuf(){
  digitalWrite(9, LOW);
  digitalWrite(8, LOW);
  digitalWrite(7, LOW);
  digitalWrite(6, LOW);
  digitalWrite(5, HIGH);
  digitalWrite(4, LOW);
  digitalWrite(3, LOW);
}

void zero(){
  digitalWrite(9, LOW);
  digitalWrite(8, LOW);
  digitalWrite(7, LOW);
  digitalWrite(6, LOW);
  digitalWrite(5, LOW);
  digitalWrite(4, LOW);
  digitalWrite(3, HIGH);
}
